# Fritzing sketch receiver (saved by Fritzing 0.9.3b)

parts:
  Composant1 = Arduino Mega 2560 (Rev3)
  Composant2 = NRF24L01+ Breakout Board
  Composant3 = Adafruit TB6612 DC and Stepper Motor Driver [part_number="Adafruit #2448"]
  M1 = DC Motor  # not connected
  M2 = DC Motor  # not connected
  YwRobot_Power_Supply1 = YwRobot Breadboard Power Supply [part_number=545043]  # not connected

nets:
  N1: Composant1.D8_PWM, Composant2.CS
  3V3: Composant1.3V3, Composant2.VCC
  5V: Composant1.5V, Composant3.VCC
  GND: Composant1.GND, Composant2.GND
  N2: Composant1.D2_PWM, Composant3.PWMA
  N3: Composant1.D3_PWM, Composant3.PWMB
  N4: Composant1.D7_PWM, Composant2.CE
  N5: Composant1.D22, Composant3.AIN1
  N6: Composant1.D23, Composant3.AIN2
  N7: Composant1.D40, Composant3.BIN1
  N8: Composant1.D41, Composant3.BIN2
  N9: Composant1.D48, Composant2.MISO
  N10: Composant1.D49, Composant2.MOSI
  N11: Composant1.D50, Composant2.SCK

custom parts:
  Adafruit TB6612 DC and Stepper Motor Driver: Spin two DC motors, step one bi-polar or uni-polar stepper, or fire off two solenoids with 1.2A per channel using the TB6612. These are perhaps better known as "the drivers in our assembled Adafruit Motorshield or Motor HAT." We really like these dual H-bridges, so if you want to control motors without a shield or HAT these are easy to include on any solderless breadboard or perma-proto.
  YwRobot Breadboard Power Supply: The YwRobot Breadboard Power Supply (MB-V2) has two power rails; they can be 5V or 3V3. Power to the module can be provided through the female USB socket or through the A10 (female) 2.1mm power jack.
