# Fritzing sketch transmitter (saved by Fritzing 0.9.3b)

parts:
  Composant1 = Arduino Mega 2560 (Rev3)
  Composant2 = NRF24L01+ Breakout Board

nets:
  N1: Composant1.D8_PWM, Composant2.CS
  3V3: Composant1.3V3, Composant2.VCC
  GND: Composant1.GND, Composant2.GND
  N2: Composant1.D7_PWM, Composant2.CE
  N3: Composant1.D48, Composant2.MISO
  N4: Composant1.D49, Composant2.MOSI
  N5: Composant1.D50, Composant2.SCK
